// Digital circuit Tentativa_1.dig as structural Verilog
module Tentativa_1 (
  input  CLK,
  input  Reset,
  input  [31:0] PC___entrada_especial,
  output [31:0] PC___saida
);

  pc #(.applicationType("IVERILOG")) u_pc (.clk(CLK), .reset(Reset), .next_pc(PC___entrada_especial), .pc(PC___saida));
endmodule

/* Code of pc:
module pc(
    input clk,
    input reset,
    input [31:0] next_pc,
    output reg [31:0] pc
);

    always @(posedge clk or posedge reset) begin
        if (reset)
            pc <= 32'b0;
        else
            pc <= next_pc;
    end
endmodule
*/
